// Logisim project control_logic.circ as structural Verilog: 1 circuit, main circuit control_logic
module control_logic (
  input  [31:0] inst,
  input  BrEq,
  input  BrLt,
  output PCSel,
  output RegWEn,
  output [2:0] ImmSel,
  output BrUn,
  output ASel,
  output BSel,
  output [3:0] ALUSel,
  output MemRW,
  output [1:0] WBSel,
  output CSRSel,
  output CSRWen
);

  wire and_1_out, and_2_out, and_3_out, and_4_out, and_7_out, and_8_out, inst2not, inst3not, inst4not,
       inst5not, inst6not, inst12not, inst13not, inst14not, inst30not, isItype, isRtype, isSBtype, isStype,
       isUJtype, isUtype;
  wire [2:0] immSelI, immSelR, immSelS, immSelSB, immSelU, immSelUJ;

  Demultiplexer #(.enable("false"), .width(3)) demultiplexer_1 (
    .out1(immSelI), .in(3'b000), .sel(isItype));  // open: out0
  and and_1 (and_1_out, inst2not, inst3not, inst4not, inst5not, inst6not);
  and and_2 (and_2_out, inst2not, inst3not, inst[4], inst5not, inst6not);
  and and_3 (and_3_out, inst[2], inst3not, inst4not, inst[5], inst[6]);
  and and_4 (and_4_out, inst2not, inst3not, inst[4], inst[5], inst[6]);
  not not_1 (inst2not, inst[2]);
  not not_2 (inst3not, inst[3]);
  not not_3 (inst4not, inst[4]);
  not not_4 (inst5not, inst[5]);
  not not_5 (inst6not, inst[6]);
  not not_6 (inst12not, inst[12]);
  not not_7 (inst13not, inst[13]);
  not not_8 (inst14not, inst[14]);
  not not_9 (inst30not, inst[30]);
  Demultiplexer #(.enable("false"), .width(3)) demultiplexer_2 (
    .out1(immSelS), .in(3'b001), .sel(isStype));  // open: out0
  or or_1 (isItype, and_1_out, and_2_out, and_3_out, and_4_out);
  Demultiplexer #(.enable("false"), .width(3)) demultiplexer_3 (
    .out1(immSelSB), .in(3'b010), .sel(isSBtype));  // open: out0
  Demultiplexer #(.enable("false"), .width(3)) demultiplexer_4 (
    .out1(immSelU), .in(3'b011), .sel(isUtype));  // open: out0
  and and_5 (isStype, inst2not, inst3not, inst4not, inst[5], inst6not);
  Demultiplexer #(.enable("false"), .width(3)) demultiplexer_5 (
    .out1(immSelUJ), .in(3'b100), .sel(isUJtype));  // open: out0
  Demultiplexer #(.enable("false"), .width(3)) demultiplexer_6 (
    .out1(immSelR), .in(3'b101), .sel(isRtype));  // open: out0
  and and_6 (isSBtype, inst2not, inst3not, inst4not, inst[5], inst[6]);
  assign ImmSel = immSelI | immSelS | immSelSB | immSelU | immSelUJ | immSelR;  // OR_Gate or_2, 3 bits wide
  and and_7 (and_7_out, inst[2], inst3not, inst[4], inst5not, inst6not);
  and and_8 (and_8_out, inst[2], inst3not, inst[4], inst[5], inst6not);
  or or_3 (isUtype, and_7_out, and_8_out);
  and and_9 (isUJtype, inst[2], inst[3], inst4not, inst[5], inst[6]);
  and and_10 (isRtype, inst2not, inst3not, inst[4], inst[5], inst6not);

  // Notes on the sheet:
  //   INPUTS to your circuit
  //   DON'T CHANGE THE LOCATIONS OF THE INPUTS AND OUTPUTS!
  //   OUTPUT from your circuit
  //   ImmSel
endmodule
